# Fritzing sketch ChuckArduino (saved by Fritzing 0.9.3b)

parts:
  Composant1 = Arduino Uno (Rev3)
  LED1 = RGB LED (com. cathode, rgb) [package="5 mm [THT]"]
  Composant2 = OLED Monochrome 128x32 I2C [part_number=931]
  U1 = POT [package=pot_mammoth]
  LED2 = RGB LED (com. cathode, rgb) [package="5 mm [THT]"]

nets:
  N1: Composant1.A1, U1.A
  N2: Composant1.A4/SDA, Composant2.SDA
  N3: Composant1.A5/SCL, Composant2.SCL
  N4: Composant1.D9_PWM, LED1.red_anode
  N5: Composant1.D10_PWM/SS, LED1.green_anode
  N6: Composant1.D11_PWM/MOSI, LED1.blue_anode
  GND: Composant1.GND, LED1.common_cathode, Composant2.GND, U1.E
  N7: Composant1.D3_PWM, LED2.red_anode
  N8: Composant1.D5_PWM, LED2.green_anode
  N9: Composant1.D6_PWM, LED2.blue_anode
  N10: Composant1.3V3, U1.S
  5V: Composant1.5V, Composant2.VIN

custom parts:
  OLED Monochrome 128x32 I2C: These displays are small, only about 1" diagonal, but very readable due to the high contrast of an OLED display. This display is made of 128x32 individual white OLED pixels, each one is turned on or off by the controller chip. Because the display makes its own light, no backlight is required. This reduces the power required to run the OLED and is why the display has such high contrast; we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
